// Logisim project LatchD.circ as structural Verilog: 1 circuit, main circuit main
module main (
  input  Data,
  input  Clock,
  output Q_negato,
  output Q
);

  wire and_1_out, and_2_out;

  and and_1 (and_1_out, Data, Clock);
  and and_2 (and_2_out, ~Data, Clock);  // AND_Gate
  nor nor_1 (Q_negato, and_1_out, Q);
  nor nor_2 (Q, Q_negato, and_2_out);
endmodule
