// Logisim project momeryCircuit.circ as structural Verilog: 1 circuit, main circuit main
module main (
  input  orderingRequest,
  input  in_2,
  input  [1:0] in_3,
  input  in_4,
  input  [1:0] in_5,
  output [1:0] out_6,
  output out_7,
  output out_8
);

  wire and_1_out, and_2_out, and_3_out, muxBottone, muxTipo, or_1_out, or_2_out, or_3_out, Select;
  wire [1:0] muxPiano;

  Multiplexer multiplexer_1 (.in0(in_2), .in1(in_4), .out(muxBottone), .sel(Select));  // open: en
  Multiplexer #(.width(2)) multiplexer_2 (.in0(in_3), .in1(in_5), .out(muxPiano), .sel(Select));  // open: en
  Multiplexer multiplexer_3 (.in0(1'b0), .in1(1'b1), .out(muxTipo), .sel(Select));  // open: en
  selector_main main_1 (.BC(in_2), .BD(in_4), .C(1'b0), .D(1'b1), .out_5(Select));
  or or_1 (or_1_out, muxBottone, orderingRequest);
  and and_1 (and_1_out, muxBottone, orderingRequest);
  and and_2 (and_2_out, or_1_out, ~and_1_out);  // AND_Gate
  and and_3 (and_3_out, ~and_2_out, and_1_out);  // AND_Gate
  or or_2 (or_2_out, and_2_out, and_3_out);
  Shift_Register #(.width(2), .length(6)) floor (
    .in(muxPiano), .clk(or_2_out), .out(out_6));  // open: shift, load, clr, d0, q0, d1, q1, d2, q2, d3, q3, d4, q4, d5, q5
  Shift_Register #(.length(6)) inOut (
    .in(muxTipo), .clk(or_2_out), .out(out_7));  // open: shift, load, clr, d0, q0, d1, q1, d2, q2, d3, q3, d4, q4, d5, q5
  or or_3 (or_3_out, in_2, in_4);
  Shift_Register #(.length(6)) valid (
    .in(or_3_out), .clk(or_2_out), .out(out_8));  // open: shift, load, clr, d0, q0, d1, q1, d2, q2, d3, q3, d4, q4, d5, q5

  // Other names for the same wires on the sheet: BC = in_2; BD = in_4; pChia[1:0] = in_3; pDest[1:0] = in_5
endmodule
