// Logisim project ordering.circ as structural Verilog: 1 circuit, main circuit main-ff
module main_ff (
  input  [1:0] floor,
  input  \type ,
  input  valid,
  input  resetByElevator,
  output f0_outC,
  output f1_outC,
  output f2_outC,
  output f3_outC,
  output f1_outD,
  output f1_outD_2,
  output f2_outD,
  output f3_outD
);

  wire activeForCaller, activeForDestination, and_4_out, and_5_out, and_6_out, and_7_out, and_8_out,
       and_9_out, and_10_out, and_11_out, data, decoder_1_out0, F0, F1, F2, F3;

  Decoder #(.select(2)) decoder_1 (.out0(decoder_1_out0), .out1(F1), .out2(F2), .out3(F3), .sel(floor));  // open: en
  or or_1 (data, valid, resetByElevator);
  and and_1 (activeForCaller, ~\type , valid);  // AND_Gate
  and and_2 (activeForDestination, \type , valid);
  and and_3 (F0, ~floor[0], ~floor[1], valid, decoder_1_out0);  // AND_Gate
  D_Flip_Flop d_ff_1 (.clk(and_4_out), .D(data), .Q(f0_outC));  // open: Qn, preset, en, reset
  and and_4 (and_4_out, activeForCaller, F0);
  and and_5 (and_5_out, activeForCaller, F1);
  D_Flip_Flop d_ff_2 (.clk(and_5_out), .D(data), .Q(f1_outC));  // open: Qn, preset, en, reset
  and and_6 (and_6_out, activeForCaller, F2);
  D_Flip_Flop d_ff_3 (.clk(and_6_out), .D(data), .Q(f2_outC));  // open: Qn, preset, en, reset
  D_Flip_Flop d_ff_4 (.clk(and_7_out), .D(data), .Q(f3_outC));  // open: Qn, preset, en, reset
  and and_7 (and_7_out, activeForCaller, F3);
  and and_8 (and_8_out, activeForDestination, F0);
  D_Flip_Flop d_ff_5 (.clk(and_8_out), .D(data), .Q(f1_outD));  // open: Qn, preset, en, reset
  and and_9 (and_9_out, activeForDestination, F1);
  D_Flip_Flop d_ff_6 (.clk(and_9_out), .D(data), .Q(f1_outD_2));  // open: Qn, preset, en, reset
  D_Flip_Flop d_ff_7 (.clk(and_10_out), .D(data), .Q(f2_outD));  // open: Qn, preset, en, reset
  and and_10 (and_10_out, activeForDestination, F2);
  D_Flip_Flop d_ff_8 (.clk(and_11_out), .D(data), .Q(f3_outD));  // open: Qn, preset, en, reset
  and and_11 (and_11_out, activeForDestination, F3);

  // Other names for the same wires on the sheet: test = valid

  // Notes on the sheet:
  //   Caller
  //   Destination
endmodule
