// Logisim project delay.circ as structural Verilog: 1 circuit, main circuit main
module main (
  input  in_1,
  input  in_2,
  output out_3,
  output out_4,
  output out_5
);

  wire and_1_out, and_2_out, and_3_out, d_ff_1_q, or_1_out, or_2_out, or_3_out, shift_register_1_q0,
       shift_register_1_q1, shift_register_1_q2, shift_register_1_q3, shift_register_1_q4,
       shift_register_2_q0, shift_register_2_q1, shift_register_2_q2, shift_register_2_q3,
       shift_register_2_q4, shift_register_3_q0, shift_register_3_q1, shift_register_3_q2,
       shift_register_3_q3, shift_register_3_q4;

  and and_1 (and_1_out, in_1, ~or_2_out);  // AND_Gate
  and and_2 (and_2_out, in_2, d_ff_1_q);
  or or_1 (or_1_out, in_1, and_2_out);
  D_Flip_Flop d_ff_1 (.clk(or_1_out), .D(and_1_out), .Q(d_ff_1_q));  // open: Qn, preset, en, reset
  or or_2 (or_2_out, shift_register_1_q0, shift_register_1_q1, shift_register_1_q2, shift_register_1_q3, shift_register_1_q4, shift_register_2_q0, shift_register_2_q1, shift_register_2_q2, shift_register_2_q3, shift_register_2_q4, shift_register_3_q0, shift_register_3_q1, shift_register_3_q2, shift_register_3_q3, shift_register_3_q4);
  and and_3 (and_3_out, in_1, or_2_out);
  or or_3 (or_3_out, d_ff_1_q, out_5);
  Shift_Register #(.length(5)) shift_register_1 (
    .in(or_3_out), .clk(in_2), .out(out_3), .clr(and_3_out), .q0(shift_register_1_q0),
    .q1(shift_register_1_q1), .q2(shift_register_1_q2), .q3(shift_register_1_q3), .q4(shift_register_1_q4));  // open: shift, load, d0, d1, d2, d3, d4
  Shift_Register #(.length(5)) shift_register_2 (
    .in(out_3), .clk(in_2), .out(out_4), .clr(and_3_out), .q0(shift_register_2_q0), .q1(shift_register_2_q1),
    .q2(shift_register_2_q2), .q3(shift_register_2_q3), .q4(shift_register_2_q4));  // open: shift, load, d0, d1, d2, d3, d4
  Shift_Register #(.length(5)) shift_register_3 (
    .in(out_4), .clk(in_2), .out(out_5), .clr(and_3_out), .q0(shift_register_3_q0), .q1(shift_register_3_q1),
    .q2(shift_register_3_q2), .q3(shift_register_3_q3), .q4(shift_register_3_q4));  // open: shift, load, d0, d1, d2, d3, d4
endmodule
