// Logisim project elevator_0.2.circ as structural Verilog: 2 circuits, main circuit main
module main (
  input  in_1,
  input  FC0,
  input  FD0,
  input  FC1,
  input  FD1,
  input  FC2,
  input  FD2,
  input  FC3,
  input  FD3,
  output [2:0] out_10
);

  wire and_1_out, and_2_out, and_3_out, and_4_out, and_5_out, and_6_out, and_7_out, and_8_out, and_9_out,
       clkActive, Clock, comparator_2_eq, comparator_3_eq, comparator_4_eq, d_ff_1_q, d_ff_2_q, d_ff_3_q,
       d_ff_4_q, multiplexer_1_out, multiplexer_2_out, multiplexer_3_out, multiplexer_4_out, or_1_out,
       or_2_out, or_3_out, or_4_out;
  wire [2:0] coutertofour_1_out_2;
  wire [7:0] bit_extender_1_out, bit_extender_2_out, bit_extender_3_out, bit_extender_4_out;

  Clock clock_1 (.out(Clock));
  couterToFour coutertofour_1 (.out_2(coutertofour_1_out_2), .in_1(Clock), .out_3(out_10));
  Comparator #(.width(3)) comparator_1 (.a(3'b000), .b(coutertofour_1_out_2), .eq(clkActive));  // open: gt, lt
  Comparator #(.width(3)) comparator_2 (.a(3'b001), .b(coutertofour_1_out_2), .eq(comparator_2_eq));  // open: gt, lt
  Comparator #(.width(3)) comparator_3 (.a(3'b010), .b(coutertofour_1_out_2), .eq(comparator_3_eq));  // open: gt, lt
  Comparator #(.width(3)) comparator_4 (.a(3'b011), .b(coutertofour_1_out_2), .eq(comparator_4_eq));  // open: gt, lt
  and and_1 (and_1_out, FC0, clkActive);
  and and_2 (and_2_out, FD0, clkActive);
  and and_3 (and_3_out, FC1, comparator_2_eq);
  and and_4 (and_4_out, FD1, comparator_2_eq);
  and and_5 (and_5_out, FC2, comparator_3_eq);
  and and_6 (and_6_out, FD2, comparator_3_eq);
  and and_7 (and_7_out, FC3, comparator_4_eq);
  and and_8 (and_8_out, FD3, comparator_4_eq);
  and and_9 (and_9_out, clkActive, Clock);
  Multiplexer multiplexer_1 (.in0(1'b0), .in1(1'b1), .out(multiplexer_1_out), .sel(or_1_out));  // open: en
  or or_1 (or_1_out, and_1_out, and_2_out);
  Multiplexer multiplexer_2 (.in0(1'b0), .in1(1'b1), .out(multiplexer_2_out), .sel(or_2_out));  // open: en
  or or_2 (or_2_out, and_3_out, and_4_out);
  Multiplexer multiplexer_3 (.in0(1'b0), .in1(1'b1), .out(multiplexer_3_out), .sel(or_3_out));  // open: en
  or or_3 (or_3_out, and_5_out, and_6_out);
  Multiplexer multiplexer_4 (.in0(1'b0), .in1(1'b1), .out(multiplexer_4_out), .sel(or_4_out));  // open: en
  or or_4 (or_4_out, and_7_out, and_8_out);
  assign bit_extender_1_out = {{7{d_ff_1_q}}, d_ff_1_q};  // Bit_Extender bit_extender_1
  D_Flip_Flop d_ff_1 (.clk(and_9_out), .D(multiplexer_1_out), .Q(d_ff_1_q));  // open: Qn, preset, en, reset
  D_Flip_Flop d_ff_2 (.clk(Clock), .D(multiplexer_2_out), .Q(d_ff_2_q));  // open: Qn, preset, en, reset
  assign bit_extender_2_out = {{7{d_ff_2_q}}, d_ff_2_q};  // Bit_Extender bit_extender_2
  assign bit_extender_3_out = {{7{d_ff_3_q}}, d_ff_3_q};  // Bit_Extender bit_extender_3
  D_Flip_Flop d_ff_3 (.clk(Clock), .D(multiplexer_3_out), .Q(d_ff_3_q));  // open: Qn, preset, en, reset
  D_Flip_Flop d_ff_4 (.clk(Clock), .D(multiplexer_4_out), .Q(d_ff_4_q));  // open: Qn, preset, en, reset
  assign bit_extender_4_out = {{7{d_ff_4_q}}, d_ff_4_q};  // Bit_Extender bit_extender_4
  DotMatrix #(.inputtype("row"), .matrixcols(8), .matrixrows(8)) dotmatrix_1 (
    .row0(bit_extender_1_out), .row1(bit_extender_1_out), .row2(bit_extender_1_out),
    .row3(bit_extender_1_out), .row4(bit_extender_1_out), .row5(bit_extender_1_out),
    .row6(bit_extender_1_out), .row7(bit_extender_1_out));
  DotMatrix #(.inputtype("row"), .matrixcols(8), .matrixrows(8)) dotmatrix_2 (
    .row0(bit_extender_2_out), .row1(bit_extender_2_out), .row2(bit_extender_2_out),
    .row3(bit_extender_2_out), .row4(bit_extender_2_out), .row5(bit_extender_2_out),
    .row6(bit_extender_2_out), .row7(bit_extender_2_out));
  DotMatrix #(.inputtype("row"), .matrixcols(8), .matrixrows(8)) dotmatrix_3 (
    .row0(bit_extender_3_out), .row1(bit_extender_3_out), .row2(bit_extender_3_out),
    .row3(bit_extender_3_out), .row4(bit_extender_3_out), .row5(bit_extender_3_out),
    .row6(bit_extender_3_out), .row7(bit_extender_3_out));
  DotMatrix #(.inputtype("row"), .matrixcols(8), .matrixrows(8)) dotmatrix_4 (
    .row0(bit_extender_4_out), .row1(bit_extender_4_out), .row2(bit_extender_4_out),
    .row3(bit_extender_4_out), .row4(bit_extender_4_out), .row5(bit_extender_4_out),
    .row6(bit_extender_4_out), .row7(bit_extender_4_out));
endmodule

module couterToFour (
  input  in_1,
  output [2:0] out_2,
  output [2:0] out_3
);

  wire and_1_out, comparator_1_eq, comparator_2_eq;
  wire [2:0] bit_extender_1_out, demultiplexer_1_out0, demultiplexer_1_out1;

  Demultiplexer #(.width(3)) demultiplexer_1 (
    .out0(demultiplexer_1_out0), .out1(demultiplexer_1_out1), .in(out_3), .sel(comparator_1_eq));  // open: en
  Counter #(.width(3), .max('h7)) counter_1 (
    .Q(out_3), .clk(in_1), .clr(comparator_2_eq));  // open: load, D, count, carry
  Comparator #(.width(3)) comparator_1 (.a(3'b100), .b(out_3), .eq(comparator_1_eq));  // open: gt, lt
  Comparator #(.width(3)) comparator_2 (.a(3'b101), .b(out_3), .eq(comparator_2_eq));  // open: gt, lt
  and and_1 (and_1_out, demultiplexer_1_out1[0], ~demultiplexer_1_out1[1], demultiplexer_1_out1[2]);  // AND_Gate
  assign bit_extender_1_out = {{2{1'b0}}, and_1_out};  // Bit_Extender bit_extender_1
  assign out_2 = demultiplexer_1_out0 | bit_extender_1_out;  // OR_Gate or_1, 3 bits wide
endmodule
