// Logisim project ordering.circ as structural Verilog: 1 circuit, main circuit main-ff
module main_ff (
  input  in_1,
  input  in_2,
  input  in_3,
  input  in_4,
  input  [1:0] floor,
  input  \type ,
  input  valid,
  input  resetByElevator,
  output f0_outC,
  output f1_outC,
  output f2_outC,
  output f3_outC,
  output f1_outD,
  output f1_outD_2,
  output f2_outD,
  output f3_outD
);

  wire activeForCaller, activeForDestination, and_4_out, and_5_out, and_6_out, and_7_out, and_8_out,
       and_9_out, and_10_out, and_11_out, and_12_out, and_13_out, and_14_out, and_15_out, and_16_out,
       and_17_out, and_18_out, and_19_out, and_20_out, and_21_out, and_22_out, and_23_out, and_24_out,
       and_25_out, and_26_out, and_27_out, and_28_out, and_29_out, and_30_out, and_31_out, and_32_out,
       and_33_out, and_34_out, and_35_out, and_36_out, and_37_out, and_38_out, and_39_out, and_40_out,
       and_41_out, and_42_out, and_43_out, data, decoder_1_out0, F0, F1, F2, F3, or_2_out, or_3_out,
       or_4_out, or_5_out, or_6_out, or_7_out, or_8_out, or_9_out, or_10_out, or_11_out, or_12_out,
       or_13_out, or_14_out, or_15_out, or_16_out, or_17_out;

  Decoder #(.select(2)) decoder_1 (.out0(decoder_1_out0), .out1(F1), .out2(F2), .out3(F3), .sel(floor));  // open: en
  and and_1 (activeForCaller, ~\type , valid);  // AND_Gate
  and and_2 (activeForDestination, \type , valid);
  or or_1 (data, valid, resetByElevator);
  and and_3 (F0, ~floor[0], ~floor[1], valid, decoder_1_out0);  // AND_Gate
  and and_4 (and_4_out, activeForCaller, F0);
  and and_5 (and_5_out, activeForCaller, F1);
  and and_6 (and_6_out, activeForCaller, F2);
  and and_7 (and_7_out, activeForCaller, F3);
  and and_8 (and_8_out, activeForDestination, F0);
  and and_9 (and_9_out, activeForDestination, F1);
  and and_10 (and_10_out, activeForDestination, F2);
  and and_11 (and_11_out, activeForDestination, F3);
  and and_12 (and_12_out, in_1, and_4_out);
  and and_13 (and_13_out, ~and_12_out, or_2_out);  // AND_Gate
  or or_2 (or_2_out, in_1, and_4_out);
  and and_14 (and_14_out, in_2, and_5_out);
  and and_15 (and_15_out, ~and_14_out, or_3_out);  // AND_Gate
  or or_3 (or_3_out, in_2, and_5_out);
  and and_16 (and_16_out, in_3, and_6_out);
  and and_17 (and_17_out, ~and_16_out, or_4_out);  // AND_Gate
  or or_4 (or_4_out, in_3, and_6_out);
  and and_18 (and_18_out, in_4, and_7_out);
  and and_19 (and_19_out, ~and_18_out, or_5_out);  // AND_Gate
  or or_5 (or_5_out, in_4, and_7_out);
  and and_20 (and_20_out, in_1, and_8_out);
  and and_21 (and_21_out, ~and_20_out, or_6_out);  // AND_Gate
  or or_6 (or_6_out, in_1, and_8_out);
  and and_22 (and_22_out, in_2, and_9_out);
  and and_23 (and_23_out, ~and_22_out, or_7_out);  // AND_Gate
  or or_7 (or_7_out, in_2, and_9_out);
  and and_24 (and_24_out, in_3, and_10_out);
  and and_25 (and_25_out, ~and_24_out, or_8_out);  // AND_Gate
  or or_8 (or_8_out, in_3, and_10_out);
  and and_26 (and_26_out, in_4, and_11_out);
  and and_27 (and_27_out, ~and_26_out, or_9_out);  // AND_Gate
  or or_9 (or_9_out, in_4, and_11_out);
  and and_28 (and_28_out, and_12_out, ~and_13_out);  // AND_Gate
  or or_10 (or_10_out, and_28_out, and_13_out);
  and and_29 (and_29_out, ~in_1, data);  // AND_Gate
  and and_30 (and_30_out, and_14_out, ~and_15_out);  // AND_Gate
  or or_11 (or_11_out, and_30_out, and_15_out);
  and and_31 (and_31_out, ~in_2, data);  // AND_Gate
  and and_32 (and_32_out, and_16_out, ~and_17_out);  // AND_Gate
  or or_12 (or_12_out, and_32_out, and_17_out);
  and and_33 (and_33_out, ~in_3, data);  // AND_Gate
  and and_34 (and_34_out, and_18_out, ~and_19_out);  // AND_Gate
  or or_13 (or_13_out, and_34_out, and_19_out);
  and and_35 (and_35_out, ~in_4, data);  // AND_Gate
  and and_36 (and_36_out, and_20_out, ~and_21_out);  // AND_Gate
  or or_14 (or_14_out, and_36_out, and_21_out);
  and and_37 (and_37_out, ~in_1, data);  // AND_Gate
  and and_38 (and_38_out, and_22_out, ~and_23_out);  // AND_Gate
  or or_15 (or_15_out, and_38_out, and_23_out);
  and and_39 (and_39_out, ~in_2, data);  // AND_Gate
  and and_40 (and_40_out, and_24_out, ~and_25_out);  // AND_Gate
  or or_16 (or_16_out, and_40_out, and_25_out);
  and and_41 (and_41_out, ~in_3, data);  // AND_Gate
  and and_42 (and_42_out, and_26_out, ~and_27_out);  // AND_Gate
  or or_17 (or_17_out, and_42_out, and_27_out);
  and and_43 (and_43_out, ~and_11_out, data);  // AND_Gate
  D_Flip_Flop d_ff_1 (.clk(or_10_out), .D(and_29_out), .Q(f0_outC));  // open: Qn, preset, en, reset
  D_Flip_Flop d_ff_2 (.clk(or_11_out), .D(and_31_out), .Q(f1_outC));  // open: Qn, preset, en, reset
  D_Flip_Flop d_ff_3 (.clk(or_12_out), .D(and_33_out), .Q(f2_outC));  // open: Qn, preset, en, reset
  D_Flip_Flop d_ff_4 (.clk(or_13_out), .D(and_35_out), .Q(f3_outC));  // open: Qn, preset, en, reset
  D_Flip_Flop d_ff_5 (.clk(or_14_out), .D(and_37_out), .Q(f1_outD));  // open: Qn, preset, en, reset
  D_Flip_Flop d_ff_6 (.clk(or_15_out), .D(and_39_out), .Q(f1_outD_2));  // open: Qn, preset, en, reset
  D_Flip_Flop d_ff_7 (.clk(or_16_out), .D(and_41_out), .Q(f2_outD));  // open: Qn, preset, en, reset
  D_Flip_Flop d_ff_8 (.clk(or_17_out), .D(and_43_out), .Q(f3_outD));  // open: Qn, preset, en, reset

  // Other names for the same wires on the sheet: resetF0 = in_1; resetF1 = in_2; resetF2 = in_3; ResetF3 = in_4;
  //   test = valid

  // Notes on the sheet:
  //   Caller
  //   Destination
  //   processed
endmodule
