// Logisim project selector.circ as structural Verilog: 1 circuit, main circuit main
module main (
  input  BC,
  input  BD,
  input  C,
  input  D,
  output out_5
);

  wire and_1_out, and_2_out, not_1_out;

  and and_1 (and_1_out, BC, ~BD, ~C, D);  // AND_Gate
  and and_2 (and_2_out, ~BC, BD, ~C, D);  // AND_Gate
  not not_1 (not_1_out, and_1_out);
  and and_3 (out_5, not_1_out, and_2_out);
endmodule
