// Logisim project elevator_1.0.circ as structural Verilog: 2 circuits, main circuit main
module main (
  input  Movement,
  input  On_Off,
  input  FC0,
  input  FD0,
  input  FC1,
  input  FD1,
  input  FC2,
  input  FD2,
  input  FC3,
  input  FD3,
  output m0Reset,
  output m1Reset,
  output m2Reset,
  output m3Reset,
  output [5:0] displayF0,
  output [5:0] displayF1,
  output [5:0] displayF2,
  output [5:0] displayF3
);

  wire activeStop0, activeStop1, activeStop2, activeStop3, and_5_out, and_6_out, and_7_out, and_8_out,
       and_9_out, and_10_out, and_11_out, and_12_out, and_13_out, and_14_out, and_15_out, and_16_out,
       comparator_1_eq, comparator_2_eq, comparator_3_eq, comparator_4_eq, F0State, or_1_out, or_2_out,
       or_3_out, or_4_out, or_5_out, or_6_out, or_7_out, or_8_out, or_9_out, or_10_out, or_11_out, or_12_out,
       or_13_out, or_14_out, or_15_out, or_16_out, or_17_out, or_18_out, or_19_out, or_20_out, resetF0,
       resetF1, resetF2, resetF3;
  wire [1:0] coutertofour_1_out_2;

  couterToFour coutertofour_1 (.out_2(coutertofour_1_out_2), .in_1(Movement));
  or or_1 (or_1_out, FC0, FD0);
  Comparator #(.width(2)) comparator_1 (.a(2'b00), .b(coutertofour_1_out_2), .eq(comparator_1_eq));  // open: gt, lt
  or or_2 (or_2_out, FC1, FD1);
  Comparator #(.width(2)) comparator_2 (.a(2'b01), .b(coutertofour_1_out_2), .eq(comparator_2_eq));  // open: gt, lt
  or or_3 (or_3_out, FC2, FD2);
  Comparator #(.width(2)) comparator_3 (.a(2'b10), .b(coutertofour_1_out_2), .eq(comparator_3_eq));  // open: gt, lt
  or or_4 (or_4_out, FC3, FD3);
  Comparator #(.width(2)) comparator_4 (.a(2'b11), .b(coutertofour_1_out_2), .eq(comparator_4_eq));  // open: gt, lt
  and and_1 (activeStop0, or_1_out, comparator_1_eq);
  and and_2 (activeStop1, or_2_out, comparator_2_eq);
  and and_3 (activeStop2, or_3_out, comparator_3_eq);
  and and_4 (activeStop3, or_4_out, comparator_4_eq);
  or or_5 (or_5_out, activeStop0, F0State);
  or or_6 (or_6_out, resetF1, activeStop1);
  or or_7 (or_7_out, resetF2, activeStop2);
  or or_8 (or_8_out, resetF3, activeStop3);
  or or_9 (or_9_out, On_Off, resetF0, or_5_out);
  or or_10 (or_10_out, On_Off, or_5_out);
  and and_5 (and_5_out, On_Off, or_6_out);
  or or_11 (or_11_out, On_Off, or_6_out);
  and and_6 (and_6_out, ~On_Off, activeStop1);  // AND_Gate
  and and_7 (and_7_out, On_Off, or_7_out);
  or or_12 (or_12_out, On_Off, or_7_out);
  and and_8 (and_8_out, ~On_Off, activeStop2);  // AND_Gate
  and and_9 (and_9_out, On_Off, or_8_out);
  or or_13 (or_13_out, On_Off, or_8_out);
  and and_10 (and_10_out, ~On_Off, activeStop3);  // AND_Gate
  D_Flip_Flop d_ff_1 (.clk(or_9_out), .D(or_10_out), .Q(m0Reset));  // open: Qn, preset, en, reset
  and and_11 (and_11_out, and_5_out, ~and_12_out);  // AND_Gate
  and and_12 (and_12_out, ~and_5_out, or_11_out);  // AND_Gate
  and and_13 (and_13_out, and_7_out, ~and_14_out);  // AND_Gate
  and and_14 (and_14_out, ~and_7_out, or_12_out);  // AND_Gate
  and and_15 (and_15_out, and_9_out, ~and_16_out);  // AND_Gate
  and and_16 (and_16_out, ~and_9_out, or_13_out);  // AND_Gate
  or or_14 (or_14_out, activeStop3, activeStop1, activeStop2);
  or or_15 (or_15_out, and_11_out, and_12_out);
  D_Flip_Flop d_ff_2 (.clk(or_15_out), .D(and_6_out), .Q(m1Reset));  // open: Qn, preset, en, reset
  or or_16 (or_16_out, and_13_out, and_14_out);
  D_Flip_Flop d_ff_3 (.clk(or_16_out), .D(and_8_out), .Q(m2Reset));  // open: Qn, preset, en, reset
  or or_17 (or_17_out, and_15_out, and_16_out);
  D_Flip_Flop d_ff_4 (.clk(or_17_out), .D(and_10_out), .Q(m3Reset));  // open: Qn, preset, en, reset
  and and_17 (resetF0, or_14_out, m0Reset);
  and and_18 (F0State, resetF0, m0Reset);
  or or_18 (or_18_out, activeStop0, activeStop2, activeStop3);
  and and_19 (resetF1, or_18_out, m1Reset);
  or or_19 (or_19_out, activeStop0, activeStop1, activeStop3);
  and and_20 (resetF2, or_19_out, m2Reset);
  or or_20 (or_20_out, activeStop0, activeStop1, activeStop2);
  and and_21 (resetF3, or_20_out, m3Reset);
  assign displayF0 = {{5{m0Reset}}, m0Reset};  // Bit_Extender bit_extender_1
  assign displayF1 = {{5{m1Reset}}, m1Reset};  // Bit_Extender bit_extender_2
  assign displayF2 = {{5{m2Reset}}, m2Reset};  // Bit_Extender bit_extender_3
  assign displayF3 = {{5{m3Reset}}, m3Reset};  // Bit_Extender bit_extender_4

  // Other names for the same wires on the sheet: Clock = Movement; displayF0_t = m0Reset; displayF1_t = m1Reset;
  //   displayF2_t = m2Reset; displayF3_t = m3Reset
endmodule

module couterToFour (
  input  in_1,
  output [1:0] out_2
);

  wire comparator_1_eq, comparator_2_eq, d_ff_1_q, or_1_out, or_2_out;

  Counter #(.width(2), .max('h3)) counter_1 (
    .load(d_ff_1_q), .count(1'b1), .Q(out_2), .clk(in_1));  // open: D, carry, clr
  Comparator #(.width(2)) comparator_1 (.a(2'b00), .b(out_2), .eq(comparator_1_eq));  // open: gt, lt
  Comparator #(.width(2)) comparator_2 (.a(2'b11), .b(out_2), .eq(comparator_2_eq));  // open: gt, lt
  or or_1 (or_1_out, comparator_1_eq, comparator_2_eq);
  or or_2 (or_2_out, comparator_2_eq, ~comparator_1_eq);  // OR_Gate
  D_Flip_Flop d_ff_1 (.clk(or_1_out), .D(or_2_out), .Q(d_ff_1_q));  // open: Qn, preset, en, reset
endmodule
