// Logisim project main_1.0.circ as structural Verilog: 2 circuits, main circuit main
module main (
  input  [1:0] in_1,
  input  [1:0] in_2
);

  wire BC, BD, chiamataP0, chiamataP1, chiamataP2, chiamataP3, clock, destinazioneP0, destinazioneP1,
       destinazioneP2, destinazioneP3, main_2_out_7, main_2_out_8, movement, ON_OFF, resetP0, resetP1,
       resetP2, resetP3;
  wire [1:0] main_2_out_6;
  wire [3:0] main_1_out_4;
  wire [5:0] Piano0, Piano1, Piano2, Piano3;

  Button button_1 (.out(ON_OFF));
  Clock clock_1 (.out(clock));
  Button button_2 (.out(BC));
  Button button_3 (.out(BD));
  delay_main main_1 (.in_1(ON_OFF), .in_2(clock), .out_4(main_1_out_4), .out_3(movement));
  DotMatrix #(.inputtype("row"), .matrixcols(4), .matrixrows(4)) dotmatrix_1 (
    .row0(main_1_out_4), .row1(main_1_out_4), .row2(main_1_out_4), .row3(main_1_out_4));
  momeryCircuit_main main_2 (
    .in_2(BC), .in_3(in_1), .in_4(BD), .in_5(in_2), .orderingRequest(clock), .out_6(main_2_out_6),
    .out_7(main_2_out_7), .out_8(main_2_out_8));
  main_ff main_ff_1 (
    .floor(main_2_out_6), .\type (main_2_out_7), .valid(main_2_out_8), .in_1(resetP0), .in_2(resetP1),
    .in_3(resetP2), .in_4(resetP3), .f0_outC(chiamataP0), .f1_outC(chiamataP1), .f2_outC(chiamataP2),
    .f3_outC(chiamataP3), .f1_outD(destinazioneP0), .f1_outD_2(destinazioneP1), .f2_outD(destinazioneP2),
    .f3_outD(destinazioneP3));
  elevator_1_0_main main_3 (
    .FC0(chiamataP0), .FD0(destinazioneP0), .FC1(chiamataP1), .FD1(destinazioneP1), .FC2(chiamataP2),
    .FD2(destinazioneP2), .FC3(chiamataP3), .FD3(destinazioneP3), .Movement(movement), .On_Off(ON_OFF),
    .m0Reset(resetP0), .m1Reset(resetP1), .m2Reset(resetP2), .m3Reset(resetP3), .displayF0(Piano0),
    .displayF1(Piano1), .displayF2(Piano2), .displayF3(Piano3));
  DotMatrix #(.inputtype("row"), .matrixcols(6), .matrixrows(6)) dotmatrix_2 (
    .row0(Piano3), .row1(Piano3), .row2(Piano3), .row3(Piano3), .row4(Piano3), .row5(Piano3));
  DotMatrix #(.inputtype("row"), .matrixcols(6), .matrixrows(6)) dotmatrix_3 (
    .row0(Piano2), .row1(Piano2), .row2(Piano2), .row3(Piano2), .row4(Piano2), .row5(Piano2));
  DotMatrix #(.inputtype("row"), .matrixcols(6), .matrixrows(6)) dotmatrix_4 (
    .row0(Piano1), .row1(Piano1), .row2(Piano1), .row3(Piano1), .row4(Piano1), .row5(Piano1));
  DotMatrix #(.inputtype("row"), .matrixcols(6), .matrixrows(6)) dotmatrix_5 (
    .row0(Piano0), .row1(Piano0), .row2(Piano0), .row3(Piano0), .row4(Piano0), .row5(Piano0));

  // Other names for the same wires on the sheet: cPiano[1:0] = in_1; dPiano[1:0] = in_2

  // Notes on the sheet:
  //   Chiamata
  //   Destinazione
endmodule

module test (
  input  [1:0] in_1,
  input  [1:0] in_2,
  input  reset,
  output f0_outC,
  output f1_outC,
  output f2_outC,
  output f3_outC,
  output f1_outD,
  output f1_outD_2,
  output f2_outD,
  output f3_outD
);

  wire activeForCaller, activeForDestination, and_1_out, and_2_out, and_3_out, and_4_out, and_5_out,
       and_6_out, and_10_out, and_11_out, and_12_out, and_13_out, and_14_out, and_15_out, and_16_out,
       and_17_out, BC, BD, button_1_out, clock, clock_1_out, d_ff_1_q, data, decoder_1_out0, F0, F1, F2, F3,
       inOut_out, muxBottone, muxTipo, or_1_out, or_2_out, or_3_out, or_4_out, or_5_out, or_6_out, Select,
       shift_register_1_out, shift_register_1_q0, shift_register_1_q1, shift_register_1_q2,
       shift_register_1_q3, shift_register_1_q4, shift_register_2_out, shift_register_2_q0,
       shift_register_2_q1, shift_register_2_q2, shift_register_2_q3, shift_register_2_q4,
       shift_register_3_out, shift_register_3_q0, shift_register_3_q1, shift_register_3_q2,
       shift_register_3_q3, shift_register_3_q4, test;
  wire [1:0] floor_out, muxPiano;

  Button button_1 (.out(button_1_out));
  Clock clock_1 (.out(clock_1_out));
  Button button_2 (.out(BC));
  Button button_3 (.out(BD));
  and and_1 (and_1_out, button_1_out, ~or_2_out);  // AND_Gate
  and and_2 (and_2_out, clock_1_out, d_ff_1_q);
  D_Flip_Flop d_ff_1 (.clk(or_1_out), .D(and_1_out), .Q(d_ff_1_q));  // open: Qn, preset, en, reset
  or or_1 (or_1_out, button_1_out, and_2_out);
  or or_2 (or_2_out, shift_register_1_q0, shift_register_1_q1, shift_register_1_q2, shift_register_1_q3, shift_register_1_q4, shift_register_2_q0, shift_register_2_q1, shift_register_2_q2, shift_register_2_q3, shift_register_2_q4, shift_register_3_q0, shift_register_3_q1, shift_register_3_q2, shift_register_3_q3, shift_register_3_q4);
  Multiplexer multiplexer_1 (.in0(BC), .in1(BD), .out(muxBottone), .sel(Select));  // open: en
  Multiplexer #(.width(2)) multiplexer_2 (.in0(in_1), .in1(in_2), .out(muxPiano), .sel(Select));  // open: en
  Multiplexer multiplexer_3 (.in0(1'b0), .in1(1'b1), .out(muxTipo), .sel(Select));  // open: en
  selector_main main_1 (.BC(BC), .BD(BD), .C(1'b0), .D(1'b1), .out_5(Select));
  and and_3 (and_3_out, button_1_out, or_2_out);
  or or_3 (or_3_out, d_ff_1_q, shift_register_3_out);
  and and_4 (and_4_out, muxBottone, clock);
  or or_4 (or_4_out, muxBottone, clock);
  and and_5 (and_5_out, or_4_out, ~and_4_out);  // AND_Gate
  and and_6 (and_6_out, ~and_5_out, and_4_out);  // AND_Gate
  or or_5 (or_5_out, and_5_out, and_6_out);
  Shift_Register #(.width(2), .length(6)) floor (
    .in(muxPiano), .clk(or_5_out), .out(floor_out));  // open: shift, load, clr, d0, q0, d1, q1, d2, q2, d3, q3, d4, q4, d5, q5
  Shift_Register #(.length(6)) inOut (
    .in(muxTipo), .clk(or_5_out), .out(inOut_out));  // open: shift, load, clr, d0, q0, d1, q1, d2, q2, d3, q3, d4, q4, d5, q5
  or or_6 (or_6_out, BC, BD);
  Shift_Register #(.length(6)) valid (
    .in(or_6_out), .clk(or_5_out), .out(test));  // open: shift, load, clr, d0, q0, d1, q1, d2, q2, d3, q3, d4, q4, d5, q5
  Shift_Register #(.length(5)) shift_register_1 (
    .in(or_3_out), .clk(clock_1_out), .out(shift_register_1_out), .clr(and_3_out), .q0(shift_register_1_q0),
    .q1(shift_register_1_q1), .q2(shift_register_1_q2), .q3(shift_register_1_q3), .q4(shift_register_1_q4));  // open: shift, load, d0, d1, d2, d3, d4
  Shift_Register #(.length(5)) shift_register_2 (
    .in(shift_register_1_out), .clk(clock_1_out), .out(shift_register_2_out), .clr(and_3_out),
    .q0(shift_register_2_q0), .q1(shift_register_2_q1), .q2(shift_register_2_q2), .q3(shift_register_2_q3),
    .q4(shift_register_2_q4));  // open: shift, load, d0, d1, d2, d3, d4
  Decoder #(.select(2)) decoder_1 (
    .out0(decoder_1_out0), .out1(F1), .out2(F2), .out3(F3), .sel(floor_out));  // open: en
  Shift_Register #(.length(5)) shift_register_3 (
    .in(shift_register_2_out), .clk(clock_1_out), .out(shift_register_3_out), .clr(and_3_out),
    .q0(shift_register_3_q0), .q1(shift_register_3_q1), .q2(shift_register_3_q2), .q3(shift_register_3_q3),
    .q4(shift_register_3_q4));  // open: shift, load, d0, d1, d2, d3, d4
  and and_7 (F0, ~floor_out[0], ~floor_out[1], test, decoder_1_out0);  // AND_Gate
  and and_8 (activeForCaller, ~inOut_out, test);  // AND_Gate
  and and_9 (activeForDestination, inOut_out, test);
  or or_7 (data, test, reset);
  or or_8 (clock, shift_register_1_out, shift_register_2_out, shift_register_3_out);
  and and_10 (and_10_out, activeForCaller, F0);
  D_Flip_Flop d_ff_2 (.clk(and_10_out), .D(data), .Q(f0_outC));  // open: Qn, preset, en, reset
  and and_11 (and_11_out, activeForCaller, F1);
  D_Flip_Flop d_ff_3 (.clk(and_11_out), .D(data), .Q(f1_outC));  // open: Qn, preset, en, reset
  and and_12 (and_12_out, activeForCaller, F2);
  D_Flip_Flop d_ff_4 (.clk(and_12_out), .D(data), .Q(f2_outC));  // open: Qn, preset, en, reset
  and and_13 (and_13_out, activeForCaller, F3);
  D_Flip_Flop d_ff_5 (.clk(and_13_out), .D(data), .Q(f3_outC));  // open: Qn, preset, en, reset
  and and_14 (and_14_out, activeForDestination, F0);
  D_Flip_Flop d_ff_6 (.clk(and_14_out), .D(data), .Q(f1_outD));  // open: Qn, preset, en, reset
  and and_15 (and_15_out, activeForDestination, F1);
  D_Flip_Flop d_ff_7 (.clk(and_15_out), .D(data), .Q(f1_outD_2));  // open: Qn, preset, en, reset
  and and_16 (and_16_out, activeForDestination, F2);
  D_Flip_Flop d_ff_8 (.clk(and_16_out), .D(data), .Q(f2_outD));  // open: Qn, preset, en, reset
  D_Flip_Flop d_ff_9 (.clk(and_17_out), .D(data), .Q(f3_outD));  // open: Qn, preset, en, reset
  and and_17 (and_17_out, activeForDestination, F3);

  // Other names for the same wires on the sheet: cPiano[1:0] = in_1; dPiano[1:0] = in_2

  // Notes on the sheet:
  //   Chiamata
  //   Destinazione
  //   Caller
  //   Destination
endmodule
